# Fritzing sketch Smart home wiring (saved by Fritzing 0.8.7b)
breadboards: 1

parts:
  Composant1 = Arduino Mega 2560 (Rev3)
  Composant2 = MQ-4
  DHT2 = DHT11 Humitidy and Temperature Sensor
  U1 = ESP8266 WiFi Module [part_number=ESP8266]
  Composant3 = Bluetooth HC-05 Macho
  부품3 = FC-28 Soil Hygrometer Module - Probe
  부품4 = FC-28 Soil Hygrometer Module

nets:
  N1: Composant1.A0, 부품4.AO
  N2: Composant1.D19/RX1, U1.GPIO_0
  N3: Composant1.D18/TX1, U1.TXD
  N4: Composant1.D17_PWM/RX2, Composant3.RXD
  N5: Composant1.D16_PWM/TX2, Composant3.TXD
  GND: Composant1.GND, Composant2.GND, DHT2.GND, U1.RXD, U1.GND, Composant3.GND, 부품4.GND
  N6: Composant1.D8_PWM, Composant2.DO
  3V3: Composant1.3V3, DHT2.VDD
  VCC: Composant1.5V, Composant2.VCC, U1.CH_PD, Composant3.VCC, 부품4.VCC
  N7: Composant1.D4_PWM, DHT2.DATA
  N8: 부품3.POS, 부품4.POS
  N9: 부품3.NEG, 부품4.NEG

custom parts:
  DHT11 Humitidy and Temperature Sensor: DHT11 Humidity and Temperature Sensor
  ESP8266 WiFi Module: Generic WiFi Module based on the ESP8266 with onboard PCB antenna and UART communications
  FC-28 Soil Hygrometer Module - Probe: The FC-28 is a soil hygrometer module that uses the Texas Instruments LM393 comparator chip to provide an analog measurement of soil humidity.
  FC-28 Soil Hygrometer Module: The FC-28 is a soil hygrometer module that uses the Texas Instruments LM393 comparator chip to provide an analog measurement of soil humidity. The digital output is high when soil moisture is over a certain threshold, as determined by adjusting the potentiometer.
