# Fritzing sketch Test_water_sensor (saved by Fritzing 0.8.7b)

parts:
  Water_Level_Sensor = Water Level Sensor
  Composant1 = Arduino Mega 2560 (Rev3)

nets:
  N1: Water_Level_Sensor.SIG, Composant1.A1
  VCC: Water_Level_Sensor.VCC, Composant1.5V
  GND: Water_Level_Sensor.GND, Composant1.GND

custom parts:
  Water Level Sensor: A water level sensor. This sensor operates at 3V to 5V. The Sig (signal) pin outputs an analogue signal that is in proportion to the amount of water in contact with the sensor.
